// Logisim project 8-Bit System.circ as structural Verilog: 18 circuits, main circuit 1-bit adder
module _1_bit_adder (
  input  In,
  input  A,
  input  B,
  output Result,
  output Out
);

  wire and_1_out, and_2_out, xor_1_out;

  and and_1 (and_1_out, A, B);
  or or_1 (Out, and_1_out, and_2_out);
  xor xor_1 (xor_1_out, A, B);
  and and_2 (and_2_out, In, xor_1_out);
  xor xor_2 (Result, In, xor_1_out);
endmodule

module _8_bit_adder (
  input  Add_Sub,
  input  [7:0] A,
  input  [7:0] B,
  output [7:0] Output,
  output Carry,
  output Overflow
);

  wire and_1_out, and_2_out, n1_bit_adder_1_out, n1_bit_adder_2_out, n1_bit_adder_3_out, n1_bit_adder_4_out,
       n1_bit_adder_5_out, n1_bit_adder_6_out, n1_bit_adder_7_out, not_1_out, not_2_out, not_3_out,
       xor_1_out, xor_2_out, xor_3_out, xor_4_out, xor_5_out, xor_6_out, xor_7_out, xor_8_out;

  xor xor_1 (xor_1_out, Add_Sub, B[0]);
  xor xor_2 (xor_2_out, B[1], Add_Sub);
  xor xor_3 (xor_3_out, B[2], Add_Sub);
  xor xor_4 (xor_4_out, B[3], Add_Sub);
  xor xor_5 (xor_5_out, B[4], Add_Sub);
  xor xor_6 (xor_6_out, B[5], Add_Sub);
  xor xor_7 (xor_7_out, B[6], Add_Sub);
  xor xor_8 (xor_8_out, B[7], Add_Sub);
  not not_1 (not_1_out, xor_8_out);
  not not_2 (not_2_out, A[2]);
  _1_bit_adder u_1_bit_adder_1 (.A(A[0]), .B(xor_1_out), .In(Add_Sub), .Out(n1_bit_adder_1_out), .Result(Output[0]));
  _1_bit_adder u_1_bit_adder_2 (
    .A(A[1]), .B(xor_2_out), .In(n1_bit_adder_1_out), .Out(n1_bit_adder_2_out), .Result(Output[1]));
  _1_bit_adder u_1_bit_adder_3 (
    .A(A[2]), .B(xor_3_out), .In(n1_bit_adder_2_out), .Out(n1_bit_adder_3_out), .Result(Output[2]));
  _1_bit_adder u_1_bit_adder_4 (
    .A(A[3]), .B(xor_4_out), .In(n1_bit_adder_3_out), .Out(n1_bit_adder_4_out), .Result(Output[3]));
  _1_bit_adder u_1_bit_adder_5 (
    .A(A[4]), .B(xor_5_out), .In(n1_bit_adder_4_out), .Out(n1_bit_adder_5_out), .Result(Output[4]));
  _1_bit_adder u_1_bit_adder_6 (
    .A(A[5]), .B(xor_6_out), .In(n1_bit_adder_5_out), .Out(n1_bit_adder_6_out), .Result(Output[5]));
  _1_bit_adder u_1_bit_adder_7 (
    .A(A[6]), .B(xor_7_out), .In(n1_bit_adder_6_out), .Out(n1_bit_adder_7_out), .Result(Output[6]));
  _1_bit_adder u_1_bit_adder_8 (.A(A[7]), .B(xor_8_out), .In(n1_bit_adder_7_out), .Out(Carry), .Result(Output[7]));
  not not_3 (not_3_out, Output[7]);
  and and_1 (and_1_out, Output[7], not_2_out, not_1_out);
  and and_2 (and_2_out, not_3_out, A[3], xor_8_out);
  or or_1 (Overflow, and_1_out, and_2_out);
endmodule

module _8_Bit_ALU (
  input  Compare,
  input  Sub,
  input  Add,
  input  Dec,
  input  Inc,
  input  Not,
  input  And,
  input  Or,
  input  Left,
  input  Right,
  input  [7:0] A,
  input  [7:0] B,
  input  Clock,
  output [7:0] Output,
  output Carry,
  output Overflow
);

  wire Addition_carry, Addition_overflow, not_1_out, or_1_out, or_2_out, or_3_out;
  wire [2:0] Equality_lesser;
  wire [7:0] Addition_output, and_1_out, bit_extender_1_out, bit_extender_2_out, controlled_buffer_1_out,
       controlled_buffer_2_out, controlled_buffer_3_out, controlled_buffer_5_out, Left_output, not_2_out,
       or_4_out, Right_output;

  assign controlled_buffer_1_out = Clock ? A : 8'bz;  // Controlled_Buffer controlled_buffer_1
  assign controlled_buffer_2_out = Clock ? B : 8'bz;  // Controlled_Buffer controlled_buffer_2
  _8_bit_equality Equality (
    .A(controlled_buffer_1_out), .B(controlled_buffer_2_out), .Lesser(Equality_lesser[0]),
    .Equal(Equality_lesser[1]), .Greater(Equality_lesser[2]));
  or or_1 (or_1_out, Sub, Add, Dec, Inc);
  assign bit_extender_1_out = {{7{1'b0}}, or_2_out};  // Bit_Extender bit_extender_1
  assign controlled_buffer_3_out = or_2_out ? bit_extender_1_out : 8'bz;  // Controlled_Buffer controlled_buffer_3
  or or_2 (or_2_out, Dec, Inc);
  not not_1 (not_1_out, or_2_out);
  or or_3 (or_3_out, not_1_out, Not);
  assign controlled_buffer_3_out = or_3_out ? controlled_buffer_2_out : 8'bz;  // Controlled_Buffer controlled_buffer_4
  assign bit_extender_2_out = {{5{1'b0}}, Equality_lesser};  // Bit_Extender bit_extender_2
  assign controlled_buffer_5_out = or_1_out ? Addition_output : 8'bz;  // Controlled_Buffer controlled_buffer_5
  _8_bit_adder Addition (
    .A(controlled_buffer_1_out), .B(controlled_buffer_3_out), .Add_Sub(Sub), .Output(Addition_output),
    .Carry(Addition_carry), .Overflow(Addition_overflow));
  assign not_2_out = ~controlled_buffer_1_out;  // NOT_Gate not_2, 8 bits wide
  assign controlled_buffer_5_out = Compare ? bit_extender_2_out : 8'bz;  // Controlled_Buffer controlled_buffer_6
  assign controlled_buffer_5_out = Not ? not_2_out : 8'bz;  // Controlled_Buffer controlled_buffer_7
  assign controlled_buffer_5_out = And ? and_1_out : 8'bz;  // Controlled_Buffer controlled_buffer_8
  assign and_1_out = controlled_buffer_1_out & controlled_buffer_3_out;  // AND_Gate and_1, 8 bits wide
  assign controlled_buffer_5_out = Or ? or_4_out : 8'bz;  // Controlled_Buffer controlled_buffer_9
  assign or_4_out = controlled_buffer_1_out | controlled_buffer_3_out;  // OR_Gate or_4, 8 bits wide
  _8_bit_left_shift u_Left (.Input(controlled_buffer_1_out), .Output(Left_output));
  _8_bit_right_shift u_Right (.Input(controlled_buffer_1_out), .Output(Right_output));
  assign controlled_buffer_5_out = Left ? Left_output : 8'bz;  // Controlled_Buffer controlled_buffer_10
  assign controlled_buffer_5_out = Right ? Right_output : 8'bz;  // Controlled_Buffer controlled_buffer_11
  assign Output = Clock ? controlled_buffer_5_out : 8'bz;  // Controlled_Buffer controlled_buffer_12
  assign Carry = Clock ? Addition_carry : 1'bz;  // Controlled_Buffer controlled_buffer_13
  assign Overflow = Clock ? Addition_overflow : 1'bz;  // Controlled_Buffer controlled_buffer_14

  // Notes on the sheet:
  //   Equality
  //   Math
  //   Logic
  //   Bit Shifting
endmodule

module _4_bit_Equality (
  input  [3:0] A,
  input  [3:0] B,
  output Lesser,
  output Equal,
  output Greater
);

  wire and_1_out, and_2_out, and_3_out, n1_bit_equality_1_equal, n1_bit_equality_1_greater,
       n1_bit_equality_2_equal, n1_bit_equality_2_greater, n1_bit_equality_3_equal,
       n1_bit_equality_3_greater, n1_bit_equality_4_equal, n1_bit_equality_4_greater;

  _1_bit_equality u_1_bit_equality_1 (
    .A(A[0]), .B(B[0]), .Equal(n1_bit_equality_1_equal), .Greater(n1_bit_equality_1_greater));  // open: Lesser
  _1_bit_equality u_1_bit_equality_2 (
    .A(A[1]), .B(B[1]), .Equal(n1_bit_equality_2_equal), .Greater(n1_bit_equality_2_greater));  // open: Lesser
  _1_bit_equality u_1_bit_equality_3 (
    .A(A[2]), .B(B[2]), .Equal(n1_bit_equality_3_equal), .Greater(n1_bit_equality_3_greater));  // open: Lesser
  _1_bit_equality u_1_bit_equality_4 (
    .A(A[3]), .B(B[3]), .Equal(n1_bit_equality_4_equal), .Greater(n1_bit_equality_4_greater));  // open: Lesser
  and and_1 (and_1_out, n1_bit_equality_1_greater, n1_bit_equality_4_equal, n1_bit_equality_3_equal, n1_bit_equality_2_equal);
  and and_2 (and_2_out, n1_bit_equality_2_greater, n1_bit_equality_3_equal, n1_bit_equality_4_equal);
  and and_3 (and_3_out, n1_bit_equality_3_greater, n1_bit_equality_4_equal);
  and and_4 (Equal, n1_bit_equality_1_equal, n1_bit_equality_2_equal, n1_bit_equality_3_equal, n1_bit_equality_4_equal);
  or or_1 (Greater, and_1_out, and_2_out, and_3_out, n1_bit_equality_4_greater);
  nor nor_1 (Lesser, Greater, Equal);

  // Notes on the sheet:
  //   4 Bit Equality
  //   builds on 1-bit equality
  //   reduced gates used by infering that A must be less than B if not equal or greater
  //   i could have built my 1-bit equality check without an output for lesser since I am not using it here, just thought that was weird
endmodule

module _1_bit_equality (
  input  A,
  input  B,
  output Lesser,
  output Equal,
  output Greater
);

  wire not_1_out, not_2_out;

  not not_1 (not_1_out, A);
  not not_2 (not_2_out, B);
  and and_1 (Lesser, not_1_out, B);
  and and_2 (Greater, A, not_2_out);
  nor nor_1 (Equal, Lesser, Greater);
endmodule

module _8_bit_equality (
  input  [7:0] A,
  input  [7:0] B,
  output Lesser,
  output Equal,
  output Greater
);

  wire and_2_out, n4_bit_equality_1_equal, n4_bit_equality_1_greater, n4_bit_equality_2_equal,
       n4_bit_equality_2_greater;

  _4_bit_Equality u_4_bit_equality_1 (
    .A(A[7:4]), .B(B[7:4]), .Equal(n4_bit_equality_1_equal), .Greater(n4_bit_equality_1_greater));  // open: Lesser
  _4_bit_Equality u_4_bit_equality_2 (
    .A(A[3:0]), .B(B[3:0]), .Equal(n4_bit_equality_2_equal), .Greater(n4_bit_equality_2_greater));  // open: Lesser
  and and_1 (Equal, n4_bit_equality_1_equal, n4_bit_equality_2_equal);
  and and_2 (and_2_out, n4_bit_equality_1_equal, n4_bit_equality_2_greater);
  or or_1 (Greater, n4_bit_equality_1_greater, and_2_out);
  nor nor_1 (Lesser, Greater, Equal);

  // Notes on the sheet:
  //   8 Bit Equality
  //   builds on 4-bit equality
  //   reduced gates used by infering that A must be less than B if not equal or greater
  //   equal
  //   i could have built my 4-bit equality check without an output for lesser since I am not using it here, just thought that was weird
  //   greater when the top 4 bits are greater
  //   or the top 4 bits are equal and bottom are greater
endmodule

module _8_bit_right_shift (
  input  [7:0] Input,
  output [7:0] Output
);


  assign Output = {1'b0, Input[7:1]};
endmodule

module _8_bit_left_shift (
  input  [7:0] Input,
  output [7:0] Output
);


  assign Output = {Input[6:0], 1'b0};
endmodule

module _8_bit_CPU (
  input  [15:0] COM,
  input  [7:0] RGG,
  input  Clock,
  output [7:0] Constant_Output_RGH,
  output [7:0] Constant_Output_RGF,
  output [7:0] Constant_Output_RGE,
  output [7:0] Constant_Output_RGD,
  output [7:0] Constant_Output_RGC
);

  wire ALU_carry, ALU_overflow, and_1_out, controlled_buffer_2_out, controlled_buffer_8_out, n8_bit_cu_1_add,
       n8_bit_cu_1_alu, n8_bit_cu_1_and, n8_bit_cu_1_cjmp, n8_bit_cu_1_cmov, n8_bit_cu_1_com,
       n8_bit_cu_1_dec, n8_bit_cu_1_gbt, n8_bit_cu_1_inc, n8_bit_cu_1_mov, n8_bit_cu_1_not, n8_bit_cu_1_orr,
       n8_bit_cu_1_sbt, n8_bit_cu_1_set, n8_bit_cu_1_slt, n8_bit_cu_1_srt, n8_bit_cu_1_sub,
       n8_bit_equality_1_equal, or_1_out;
  wire [7:0] ALU_output, controlled_buffer_1_out, controlled_buffer_3_out, controlled_buffer_4_out,
       controlled_buffer_5_out, controlled_buffer_6_out, n8_bit_constant_swap_1_input,
       n8_bit_constant_swap_1_reg_a_2, n8_bit_constant_swap_1_reg_b_2, n8_bit_constant_swap_1_reg_c_2,
       n8_bit_cu_1_input_constant, n8_bit_cu_1_input_register_a, n8_bit_cu_1_input_register_b,
       n8_bit_cu_1_output_register_c, n8_bit_register_bank_1_output_register_a,
       n8_bit_register_bank_1_output_register_b;

  _8_bit_CU u_8_bit_cu_1 (
    .COM(n8_bit_cu_1_com), .SUB(n8_bit_cu_1_sub), .ADD(n8_bit_cu_1_add), .DEC(n8_bit_cu_1_dec),
    .INC(n8_bit_cu_1_inc), .NOT(n8_bit_cu_1_not), .AND(n8_bit_cu_1_and), .ORR(n8_bit_cu_1_orr),
    .SLT(n8_bit_cu_1_slt), .SRT(n8_bit_cu_1_srt), .ALU(n8_bit_cu_1_alu),
    .Input_Register_A(n8_bit_cu_1_input_register_a), .Input_Register_B(n8_bit_cu_1_input_register_b),
    .Output_Register_C(n8_bit_cu_1_output_register_c), .Command(COM), .SET(n8_bit_cu_1_set),
    .SBT(n8_bit_cu_1_sbt), .GBT(n8_bit_cu_1_gbt), .CMOV(n8_bit_cu_1_cmov), .CJMP(n8_bit_cu_1_cjmp),
    .MOV(n8_bit_cu_1_mov), .Input_Constant(n8_bit_cu_1_input_constant), .Clock(Clock));
  _8_bit_constant_swap u_8_bit_constant_swap_1 (
    .SET(n8_bit_cu_1_set), .CJMP(n8_bit_cu_1_cjmp), .Input_Constant(n8_bit_cu_1_input_constant),
    .Input_Value(controlled_buffer_1_out), .Reg_A(n8_bit_cu_1_input_register_a),
    .Reg_B(n8_bit_cu_1_input_register_b), .Reg_C(n8_bit_cu_1_output_register_c),
    .Input(n8_bit_constant_swap_1_input), .Reg_A_2(n8_bit_constant_swap_1_reg_a_2),
    .Reg_B_2(n8_bit_constant_swap_1_reg_b_2), .Reg_C_2(n8_bit_constant_swap_1_reg_c_2),
    .CJMP_Active(controlled_buffer_2_out), .CMOV(n8_bit_cu_1_cmov),
    .A_Value(n8_bit_register_bank_1_output_register_a), .B_Value(n8_bit_register_bank_1_output_register_b));
  assign controlled_buffer_1_out = Clock ? controlled_buffer_4_out : 8'bz;  // Controlled_Buffer controlled_buffer_1
  assign controlled_buffer_2_out = Clock ? and_1_out : 1'bz;  // Controlled_Buffer controlled_buffer_2
  _8_bit_register_bank u_8_bit_register_bank_1 (
    .Input(n8_bit_constant_swap_1_input), .Input_Register(n8_bit_constant_swap_1_reg_c_2),
    .Register_A(n8_bit_constant_swap_1_reg_a_2), .Clock(Clock), .Register_B(n8_bit_constant_swap_1_reg_b_2),
    .Output_Register_A(n8_bit_register_bank_1_output_register_a),
    .Output_Register_B(n8_bit_register_bank_1_output_register_b), .Constant_Input_RGG(RGG),
    .Constant_Output_RGH(Constant_Output_RGH), .Constant_Output_RGF(Constant_Output_RGF),
    .Constant_Output_RGE(Constant_Output_RGE), .Constant_Output_RGD(Constant_Output_RGD),
    .Constant_Output_RGC(Constant_Output_RGC));  // open: Constant_Output_RGB, Constant_Output_RGA
  assign controlled_buffer_3_out = n8_bit_cu_1_alu ? n8_bit_register_bank_1_output_register_a : 8'bz;  // Controlled_Buffer controlled_buffer_3
  assign controlled_buffer_4_out = n8_bit_cu_1_mov ? n8_bit_register_bank_1_output_register_a : 8'bz;  // Controlled_Buffer controlled_buffer_4
  assign controlled_buffer_5_out = Clock ? controlled_buffer_3_out : 8'bz;  // Controlled_Buffer controlled_buffer_5
  assign controlled_buffer_6_out = Clock ? n8_bit_register_bank_1_output_register_b : 8'bz;  // Controlled_Buffer controlled_buffer_6
  assign controlled_buffer_4_out = n8_bit_cu_1_alu ? ALU_output : 8'bz;  // Controlled_Buffer controlled_buffer_7
  _8_Bit_ALU ALU (
    .A(controlled_buffer_5_out), .B(controlled_buffer_6_out), .Compare(n8_bit_cu_1_com),
    .Sub(n8_bit_cu_1_sub), .Add(n8_bit_cu_1_add), .Dec(n8_bit_cu_1_dec), .Inc(n8_bit_cu_1_inc),
    .Not(n8_bit_cu_1_not), .And(n8_bit_cu_1_and), .Or(n8_bit_cu_1_orr), .Left(n8_bit_cu_1_slt),
    .Right(n8_bit_cu_1_srt), .Clock(Clock), .Output(ALU_output), .Carry(ALU_carry), .Overflow(ALU_overflow));
  or or_1 (or_1_out, ALU_carry, ALU_overflow);
  LED led_1 (.in(controlled_buffer_8_out));
  assign controlled_buffer_8_out = Clock ? or_1_out : 1'bz;  // Controlled_Buffer controlled_buffer_8
  _8_bit_equality u_8_bit_equality_1 (
    .A(n8_bit_register_bank_1_output_register_a), .B(8'h2), .Equal(n8_bit_equality_1_equal));  // open: Lesser, Greater
  and and_1 (and_1_out, n8_bit_equality_1_equal, n8_bit_cu_1_cjmp);
endmodule

// Control Unit
module _8_bit_CU (
  input  [15:0] Command,
  input  Clock,
  output COM,
  output SUB,
  output ADD,
  output DEC,
  output INC,
  output NOT,
  output AND,
  output ORR,
  output SLT,
  output SRT,
  output ALU,
  output MOV,
  output SET,
  output SBT,
  output GBT,
  output CMOV,
  output CJMP,
  output [7:0] Input_Constant,
  output [7:0] Input_Register_A,
  output [7:0] Input_Register_B,
  output [7:0] Output_Register_C
);

  wire or_1_out, or_2_out;
  wire [7:0] controlled_buffer_1_out;

  Demultiplexer #(.select(3)) demultiplexer_1 (
    .out0(Input_Register_A[0]), .out1(Input_Register_A[1]), .out2(Input_Register_A[2]),
    .out3(Input_Register_A[3]), .out4(Input_Register_A[4]), .out5(Input_Register_A[5]),
    .out6(Input_Register_A[6]), .out7(Input_Register_A[7]), .in(1'b1), .sel(Command[11:9]));  // open: en
  Demultiplexer #(.select(3)) demultiplexer_2 (
    .out0(Input_Register_B[0]), .out1(Input_Register_B[1]), .out2(Input_Register_B[2]),
    .out3(Input_Register_B[3]), .out4(Input_Register_B[4]), .out5(Input_Register_B[5]),
    .out6(Input_Register_B[6]), .out7(Input_Register_B[7]), .in(1'b1), .sel(Command[7:5]));  // open: en
  Demultiplexer #(.select(3)) demultiplexer_3 (
    .out0(Output_Register_C[0]), .out1(Output_Register_C[1]), .out2(Output_Register_C[2]),
    .out3(Output_Register_C[3]), .out4(Output_Register_C[4]), .out5(Output_Register_C[5]),
    .out6(Output_Register_C[6]), .out7(Output_Register_C[7]), .in(1'b1), .sel(Command[3:1]));  // open: en
  or or_1 (or_1_out, SET, CJMP);
  assign controlled_buffer_1_out = or_1_out ? Command[11:4] : 8'bz;  // Controlled_Buffer controlled_buffer_1
  assign Input_Constant = Clock ? controlled_buffer_1_out : 8'bz;  // Controlled_Buffer controlled_buffer_2
  Demultiplexer #(.select(4), .disabled(0)) demultiplexer_4 (
    .out0(COM), .out1(SUB), .out2(ADD), .out3(DEC), .out4(INC), .out5(NOT), .out6(AND), .out7(ORR),
    .out8(SLT), .out9(SRT), .out10(MOV), .out11(SET), .out12(SBT), .out13(GBT), .out14(CMOV), .out15(CJMP),
    .in(1'b1), .sel(Command[15:12]));  // open: en
  or or_2 (or_2_out, MOV, SET, SBT, GBT, CMOV, CJMP);
  assign ALU = Clock ? ~or_2_out : 1'bz;  // Controlled_Inverter controlled_inverter_1

  // Notes on the sheet:
  //   First 4 Bits - Operation
  //   Second 4 Bits - Register A
  //   Third 4 Bits - Register B
  //   Final 4 Bits - Register C
endmodule

// Registers
module _8_bit_register_bank (
  input  [7:0] Constant_Input_RGG,
  input  [7:0] Input,
  input  [7:0] Input_Register,
  input  [7:0] Register_A,
  input  Clock,
  input  [7:0] Register_B,
  output [7:0] Constant_Output_RGH,
  output [7:0] Constant_Output_RGF,
  output [7:0] Constant_Output_RGE,
  output [7:0] Constant_Output_RGD,
  output [7:0] Constant_Output_RGC,
  output [7:0] Constant_Output_RGB,
  output [7:0] Constant_Output_RGA,
  output [7:0] Output_Register_A,
  output [7:0] Output_Register_B
);

  wire n8_bit_register_writer_1_write_a, n8_bit_register_writer_1_write_b, n8_bit_register_writer_1_write_c,
       n8_bit_register_writer_1_write_d, n8_bit_register_writer_1_write_e, n8_bit_register_writer_1_write_f,
       n8_bit_register_writer_1_write_h, not_1_out, not_2_out;
  wire [7:0] controlled_buffer_1_out, controlled_buffer_2_out, n8_bit_register_writer_1_input_a,
       n8_bit_register_writer_1_input_b, n8_bit_register_writer_1_input_c, n8_bit_register_writer_1_input_d,
       n8_bit_register_writer_1_input_e, n8_bit_register_writer_1_input_f, n8_bit_register_writer_1_input_h;

  _8_bit_register_writer u_8_bit_register_writer_1 (
    .Input(controlled_buffer_1_out), .Register_Address(Input_Register),
    .Input_H(n8_bit_register_writer_1_input_h), .Write_H(n8_bit_register_writer_1_write_h),
    .Input_F(n8_bit_register_writer_1_input_f), .Write_F(n8_bit_register_writer_1_write_f),
    .Input_E(n8_bit_register_writer_1_input_e), .Write_E(n8_bit_register_writer_1_write_e),
    .Input_D(n8_bit_register_writer_1_input_d), .Write_D(n8_bit_register_writer_1_write_d),
    .Input_C(n8_bit_register_writer_1_input_c), .Write_C(n8_bit_register_writer_1_write_c),
    .Input_B(n8_bit_register_writer_1_input_b), .Write_B(n8_bit_register_writer_1_write_b),
    .Input_A(n8_bit_register_writer_1_input_a), .Write_A(n8_bit_register_writer_1_write_a));  // open: Input_G, Write_G
  assign controlled_buffer_1_out = Clock ? Input : 8'bz;  // Controlled_Buffer controlled_buffer_1
  assign controlled_buffer_2_out = n8_bit_register_writer_1_write_h ? n8_bit_register_writer_1_input_h : 8'bz;  // Controlled_Buffer controlled_buffer_2
  not not_1 (not_1_out, Clock);
  not not_2 (not_2_out, n8_bit_register_writer_1_write_h);
  assign Output_Register_A = Register_A[7] ? Constant_Output_RGH : 8'bz;  // Controlled_Buffer controlled_buffer_3
  Counter #(.trigger("falling")) counter_1 (
    .load(n8_bit_register_writer_1_write_h), .D(controlled_buffer_2_out), .count(not_2_out),
    .Q(Constant_Output_RGH), .clk(Clock));  // open: carry, clr
  assign Output_Register_A = Register_A[6] ? Constant_Input_RGG : 8'bz;  // Controlled_Buffer controlled_buffer_4
  _8_bit_register RF (
    .Input(n8_bit_register_writer_1_input_f), .Write(n8_bit_register_writer_1_write_f), .A(Register_A[5]),
    .B(Register_B[5]), .Clock(not_1_out), .Constant_Output(Constant_Output_RGF),
    .A_Output(Output_Register_A), .B_Output(Output_Register_B));
  _8_bit_register RE (
    .Input(n8_bit_register_writer_1_input_e), .Write(n8_bit_register_writer_1_write_e), .A(Register_A[4]),
    .B(Register_B[4]), .Clock(not_1_out), .Constant_Output(Constant_Output_RGE),
    .A_Output(Output_Register_A), .B_Output(Output_Register_B));
  _8_bit_register RD (
    .Input(n8_bit_register_writer_1_input_d), .Write(n8_bit_register_writer_1_write_d), .A(Register_A[3]),
    .B(Register_B[3]), .Clock(not_1_out), .Constant_Output(Constant_Output_RGD),
    .A_Output(Output_Register_A), .B_Output(Output_Register_B));
  _8_bit_register RC (
    .Input(n8_bit_register_writer_1_input_c), .Write(n8_bit_register_writer_1_write_c), .A(Register_A[2]),
    .B(Register_B[2]), .Clock(not_1_out), .Constant_Output(Constant_Output_RGC),
    .A_Output(Output_Register_A), .B_Output(Output_Register_B));
  _8_bit_register RB (
    .Input(n8_bit_register_writer_1_input_b), .Write(n8_bit_register_writer_1_write_b), .A(Register_A[1]),
    .B(Register_B[1]), .Clock(not_1_out), .Constant_Output(Constant_Output_RGB),
    .A_Output(Output_Register_A), .B_Output(Output_Register_B));
  _8_bit_register RA (
    .Input(n8_bit_register_writer_1_input_a), .Write(n8_bit_register_writer_1_write_a), .A(Register_A[0]),
    .B(Register_B[0]), .Clock(not_1_out), .Constant_Output(Constant_Output_RGA),
    .A_Output(Output_Register_A), .B_Output(Output_Register_B));
  assign Output_Register_B = Register_B[7] ? Constant_Output_RGH : 8'bz;  // Controlled_Buffer controlled_buffer_5
  assign Output_Register_B = Register_B[6] ? Constant_Input_RGG : 8'bz;  // Controlled_Buffer controlled_buffer_6
endmodule

module _8_bit_register_writer (
  input  [7:0] Input,
  input  [7:0] Register_Address,
  output [7:0] Input_H,
  output Write_H,
  output [7:0] Input_G,
  output Write_G,
  output [7:0] Input_F,
  output Write_F,
  output [7:0] Input_E,
  output Write_E,
  output [7:0] Input_D,
  output Write_D,
  output [7:0] Input_C,
  output Write_C,
  output [7:0] Input_B,
  output Write_B,
  output [7:0] Input_A,
  output Write_A
);

  assign Input_H = Register_Address[7] ? Input : 8'bz;  // Controlled_Buffer controlled_buffer_1
  assign Input_G = Register_Address[6] ? Input : 8'bz;  // Controlled_Buffer controlled_buffer_2
  assign Input_F = Register_Address[5] ? Input : 8'bz;  // Controlled_Buffer controlled_buffer_3
  assign Input_E = Register_Address[4] ? Input : 8'bz;  // Controlled_Buffer controlled_buffer_4
  assign Input_D = Register_Address[3] ? Input : 8'bz;  // Controlled_Buffer controlled_buffer_5
  assign Input_C = Register_Address[2] ? Input : 8'bz;  // Controlled_Buffer controlled_buffer_6
  assign Input_B = Register_Address[1] ? Input : 8'bz;  // Controlled_Buffer controlled_buffer_7
  assign Input_A = Register_Address[0] ? Input : 8'bz;  // Controlled_Buffer controlled_buffer_8

  assign Write_A = Register_Address[0];
  assign Write_B = Register_Address[1];
  assign Write_C = Register_Address[2];
  assign Write_D = Register_Address[3];
  assign Write_E = Register_Address[4];
  assign Write_F = Register_Address[5];
  assign Write_G = Register_Address[6];
  assign Write_H = Register_Address[7];
endmodule

module _8_bit_system (
);

  wire Clock_out, n8_bit_from_ascii_1_clear_input, n8_bit_to_ascii_1_enabled;
  wire [6:0] keyboard_1_data, n8_bit_to_ascii_1_ascii_output;
  wire [7:0] n8_bit_cpu_1_constant_output_rgc, n8_bit_cpu_1_constant_output_rgd,
       n8_bit_cpu_1_constant_output_rge, n8_bit_cpu_1_constant_output_rgf, n8_bit_cpu_1_constant_output_rgh,
       n8_bit_from_ascii_1__8_bit_output;
  wire [15:0] rom_1_data;

  Clock Clock (.out(Clock_out));
  ROM #(.dataWidth(16)) rom_1 (.addr(n8_bit_cpu_1_constant_output_rgh), .data(rom_1_data), .sel(Clock_out));
  _8_bit_CPU u_8_bit_cpu_1 (
    .COM(rom_1_data), .RGG(n8_bit_from_ascii_1__8_bit_output),
    .Constant_Output_RGH(n8_bit_cpu_1_constant_output_rgh), .Clock(Clock_out),
    .Constant_Output_RGF(n8_bit_cpu_1_constant_output_rgf),
    .Constant_Output_RGE(n8_bit_cpu_1_constant_output_rge),
    .Constant_Output_RGD(n8_bit_cpu_1_constant_output_rgd),
    .Constant_Output_RGC(n8_bit_cpu_1_constant_output_rgc));
  _8_bit_to_ASCII u_8_bit_to_ascii_1 (
    .in_1(n8_bit_cpu_1_constant_output_rgf), .Clock(Clock_out),
    .ASCII_Output(n8_bit_to_ascii_1_ascii_output), .Enabled(n8_bit_to_ascii_1_enabled));  // open: Clear
  TTY tty_1 (.data(n8_bit_to_ascii_1_ascii_output), .clk(n8_bit_to_ascii_1_enabled));  // open: we, clr
  DotMatrix #(.inputtype("row"), .matrixcols(8), .matrixrows(4), .dotshape("circle")) dotmatrix_1 (
    .row0(n8_bit_cpu_1_constant_output_rgf), .row1(n8_bit_cpu_1_constant_output_rge),
    .row2(n8_bit_cpu_1_constant_output_rgd), .row3(n8_bit_cpu_1_constant_output_rgc));
  Keyboard #(.buflen(1)) keyboard_1 (
    .clr(n8_bit_from_ascii_1_clear_input), .data(keyboard_1_data));  // open: clk, re, avail
  _8_bit_from_ASCII u_8_bit_from_ascii_1 (
    .in_1(keyboard_1_data), .Clear(n8_bit_to_ascii_1_enabled),
    ._8_bit_Output(n8_bit_from_ascii_1__8_bit_output), .Clear_Input(n8_bit_from_ascii_1_clear_input));

  // Notes on the sheet:
  //   app ROM
  //   dedicated ROM address register RH
  //   COMMAND
  //   contents of rom_1 (hex, n*v repeats v):
  //   b004 b038 b48e b058 b35e bff6 466 f0f6 b012 6246 626 8606 f166 9404 b03e b4fa b4ea b45a b53a b0aa
  //   b00a b00e b4ca b53a b42a b3da b30a b0aa b00a b00e bff0 400 f0f0 9404 b010 6402 22 8202 f162 b03e
  //   b4fa b4ea b45a b53a b0aa b00e b4ca b53a b42a b3da b30a b0aa b00e b800 6042 22 f3c2 b30a b00a b3fe
  //   b31a b00a b3fe 9000 b002 22 f442 b36e b0aa b00a b022 e82e 0 b000 c00 f480 0 b0a0 c00 f880 0 b300 c00
  //   8000 f5b0 0 b390 c00 9000 f5b0 b5fe 0 b80a b00a b48e 0 b000 400 9000 f670 b300 1c04 b83e 0 b090 400
  //   9000 f770 0 8404 a402 8404 2424 8202 2424 b300 1c00 2044 b83e 0 0 8404 a402 8404 2424 8202 2424 b300
  //   1c00 2404 b88e 0 b800 2c0a b00a b48e 0 ac0a b8aa b00a b020 e80e
  //   8-bit to ascii
  //   ascii to 8-bit
endmodule

module _8_bit_to_ASCII (
  input  [7:0] in_1,
  input  Clock,
  output [6:0] ASCII_Output,
  output Clear,
  output Enabled
);

  wire or_1_out;

  or or_1 (or_1_out, in_1[0], in_1[1], in_1[2], in_1[3], in_1[4], in_1[5], in_1[6]);
  and and_1 (Enabled, or_1_out, Clock);

  assign ASCII_Output = in_1[6:0];
  assign Clear = in_1[7];

  // Notes on the sheet:
  //   ASCII output is only 7 bits, but our register values are 8-bit.
  //   The extra bit is used as the clear flag. If no bits are set
  //   The enabled flag is not set. This mechanism simplifies outter wiring with 
endmodule

module _8_bit_from_ASCII (
  input  [6:0] in_1,
  input  Clear,
  output [7:0] _8_bit_Output,
  output Clear_Input
);


  assign _8_bit_Output = {1'b0, in_1};
  assign Clear_Input = Clear;

  // Notes on the sheet:
  //   ASCII input is only 7 bits, but our register values are 8-bit.
endmodule

module _8_bit_register (
  input  [7:0] Input,
  input  Write,
  input  A,
  input  B,
  input  Clock,
  output [7:0] Constant_Output,
  output [7:0] A_Output,
  output [7:0] B_Output
);

  Register #(.trigger("high")) Flip_Flop (.D(Input), .en(Write), .Q(Constant_Output), .clk(Clock));  // open: clr
  assign A_Output = A ? Constant_Output : 8'bz;  // Controlled_Buffer controlled_buffer_1
  assign B_Output = B ? Constant_Output : 8'bz;  // Controlled_Buffer controlled_buffer_2
endmodule

// Swapper
module _8_bit_constant_swap (
  input  CMOV,
  input  SET,
  input  CJMP,
  input  [7:0] Input_Constant,
  input  [7:0] Input_Value,
  input  [7:0] Reg_A,
  input  [7:0] Reg_B,
  input  [7:0] Reg_C,
  input  CJMP_Active,
  input  [7:0] A_Value,
  input  [7:0] B_Value,
  output [7:0] Input,
  output [7:0] Reg_A_2,
  output [7:0] Reg_B_2,
  output [7:0] Reg_C_2
);

  wire and_1_out, n8_bit_equality_1_equal, not_1_out, not_2_out, not_3_out, not_4_out, or_1_out, or_2_out;
  wire [7:0] controlled_buffer_1_out, controlled_buffer_2_out, controlled_buffer_6_out;

  assign controlled_buffer_1_out = CJMP ? 8'h80 : 8'bz;  // Controlled_Buffer controlled_buffer_1
  or or_1 (or_1_out, SET, CJMP);
  not not_1 (not_1_out, CJMP);
  assign controlled_buffer_2_out = not_1_out ? Reg_C : 8'bz;  // Controlled_Buffer controlled_buffer_2
  assign Reg_A_2 = CJMP ? Reg_C : 8'bz;  // Controlled_Buffer controlled_buffer_3
  not not_2 (not_2_out, or_1_out);
  assign Input = or_1_out ? Input_Constant : 8'bz;  // Controlled_Buffer controlled_buffer_4
  assign Reg_A_2 = not_1_out ? Reg_A : 8'bz;  // Controlled_Buffer controlled_buffer_5
  not not_3 (not_3_out, CMOV);
  assign controlled_buffer_6_out = not_2_out ? Input_Value : 8'bz;  // Controlled_Buffer controlled_buffer_6
  assign Input = not_3_out ? controlled_buffer_6_out : 8'bz;  // Controlled_Buffer controlled_buffer_7
  assign Reg_C_2 = or_2_out ? controlled_buffer_2_out : 8'bz;  // Controlled_Buffer controlled_buffer_8
  assign Reg_C_2 = CJMP_Active ? controlled_buffer_1_out : 8'bz;  // Controlled_Buffer controlled_buffer_9
  or or_2 (or_2_out, not_4_out, and_1_out);
  not not_4 (not_4_out, CMOV);
  and and_1 (and_1_out, CMOV, n8_bit_equality_1_equal);
  _8_bit_equality u_8_bit_equality_1 (.A(B_Value), .B(8'h2), .Equal(n8_bit_equality_1_equal));  // open: Lesser, Greater
  assign Input = CMOV ? A_Value : 8'bz;  // Controlled_Buffer controlled_buffer_10

  assign Reg_B_2 = Reg_B;

  // Notes on the sheet:
  //   SET and CJMP use input constant
  //   all others use input value
  //   SET C to A WHEN B = 2
endmodule

module test (
  input  Clock,
  output [7:0] Constant_Output_RGH,
  output [7:0] Constant_Output_RGF,
  output [7:0] Reg_A,
  output [7:0] Constant_Output_RGE,
  output [7:0] Reg_B,
  output [7:0] Constant_Output_RGD,
  output [7:0] Input,
  output [7:0] Constant_Output_RGC,
  output [7:0] Reg_C
);

  wire ALU_carry, ALU_overflow, and_1_out, controlled_buffer_9_out, controlled_buffer_15_out,
       n8_bit_cu_1_add, n8_bit_cu_1_alu, n8_bit_cu_1_and, n8_bit_cu_1_cjmp, n8_bit_cu_1_cmov,
       n8_bit_cu_1_com, n8_bit_cu_1_dec, n8_bit_cu_1_gbt, n8_bit_cu_1_inc, n8_bit_cu_1_mov, n8_bit_cu_1_not,
       n8_bit_cu_1_orr, n8_bit_cu_1_sbt, n8_bit_cu_1_set, n8_bit_cu_1_slt, n8_bit_cu_1_srt, n8_bit_cu_1_sub,
       n8_bit_equality_1_equal, not_1_out, or_1_out, or_2_out;
  wire [7:0] ALU_output, controlled_buffer_1_out, controlled_buffer_2_out, controlled_buffer_4_out,
       controlled_buffer_6_out, controlled_buffer_8_out, controlled_buffer_10_out, controlled_buffer_12_out,
       controlled_buffer_13_out, n8_bit_cu_1_input_constant, n8_bit_cu_1_input_register_a,
       n8_bit_cu_1_input_register_b, n8_bit_cu_1_output_register_c, n8_bit_register_bank_1_output_register_a,
       n8_bit_register_bank_1_output_register_b, undriven_2;
  wire [15:0] undriven;

  _8_bit_CU u_8_bit_cu_1 (
    .COM(n8_bit_cu_1_com), .SUB(n8_bit_cu_1_sub), .ADD(n8_bit_cu_1_add), .DEC(n8_bit_cu_1_dec),
    .INC(n8_bit_cu_1_inc), .NOT(n8_bit_cu_1_not), .AND(n8_bit_cu_1_and), .ORR(n8_bit_cu_1_orr),
    .SLT(n8_bit_cu_1_slt), .SRT(n8_bit_cu_1_srt), .ALU(n8_bit_cu_1_alu),
    .Input_Register_A(n8_bit_cu_1_input_register_a), .Input_Register_B(n8_bit_cu_1_input_register_b),
    .Output_Register_C(n8_bit_cu_1_output_register_c), .Command(undriven), .SET(n8_bit_cu_1_set),
    .SBT(n8_bit_cu_1_sbt), .GBT(n8_bit_cu_1_gbt), .CMOV(n8_bit_cu_1_cmov), .CJMP(n8_bit_cu_1_cjmp),
    .MOV(n8_bit_cu_1_mov), .Input_Constant(n8_bit_cu_1_input_constant), .Clock(Clock));
  _8_bit_constant_swap u_8_bit_constant_swap_1 ();  // open: SET, CJMP, Input_Constant, Input_Value, Reg_A, Reg_B, Reg_C, Input, Reg_A_2, Reg_B_2, Reg_C_2, CJMP_Active, CMOV, A_Value, B_Value
  not not_1 (not_1_out, n8_bit_cu_1_cjmp);
  assign controlled_buffer_1_out = not_1_out ? n8_bit_cu_1_input_register_a : 8'bz;  // Controlled_Buffer controlled_buffer_1
  assign controlled_buffer_2_out = not_1_out ? n8_bit_cu_1_output_register_c : 8'bz;  // Controlled_Buffer controlled_buffer_2
  assign controlled_buffer_2_out = controlled_buffer_9_out ? 8'h80 : 8'bz;  // Controlled_Buffer controlled_buffer_3
  assign controlled_buffer_4_out = controlled_buffer_9_out ? n8_bit_cu_1_input_constant : 8'bz;  // Controlled_Buffer controlled_buffer_4
  assign controlled_buffer_1_out = n8_bit_cu_1_cjmp ? n8_bit_cu_1_output_register_c : 8'bz;  // Controlled_Buffer controlled_buffer_5
  assign controlled_buffer_6_out = or_1_out ? controlled_buffer_2_out : 8'bz;  // Controlled_Buffer controlled_buffer_6
  assign controlled_buffer_4_out = Clock ? controlled_buffer_8_out : 8'bz;  // Controlled_Buffer controlled_buffer_7
  assign controlled_buffer_8_out = n8_bit_cu_1_set ? n8_bit_cu_1_input_constant : 8'bz;  // Controlled_Buffer controlled_buffer_8
  or or_1 (or_1_out, n8_bit_cu_1_set, n8_bit_cu_1_alu, and_1_out, n8_bit_cu_1_mov);
  assign controlled_buffer_9_out = Clock ? and_1_out : 1'bz;  // Controlled_Buffer controlled_buffer_9
  _8_bit_register_bank u_8_bit_register_bank_1 (
    .Input(controlled_buffer_4_out), .Input_Register(controlled_buffer_6_out),
    .Register_A(controlled_buffer_1_out), .Clock(Clock), .Register_B(n8_bit_cu_1_input_register_b),
    .Output_Register_A(n8_bit_register_bank_1_output_register_a),
    .Output_Register_B(n8_bit_register_bank_1_output_register_b), .Constant_Input_RGG(undriven_2),
    .Constant_Output_RGH(Constant_Output_RGH), .Constant_Output_RGF(Constant_Output_RGF),
    .Constant_Output_RGE(Constant_Output_RGE), .Constant_Output_RGD(Constant_Output_RGD),
    .Constant_Output_RGC(Constant_Output_RGC));  // open: Constant_Output_RGB, Constant_Output_RGA
  assign controlled_buffer_10_out = n8_bit_cu_1_alu ? n8_bit_register_bank_1_output_register_a : 8'bz;  // Controlled_Buffer controlled_buffer_10
  assign controlled_buffer_8_out = n8_bit_cu_1_mov ? n8_bit_register_bank_1_output_register_a : 8'bz;  // Controlled_Buffer controlled_buffer_11
  assign controlled_buffer_12_out = Clock ? controlled_buffer_10_out : 8'bz;  // Controlled_Buffer controlled_buffer_12
  assign controlled_buffer_13_out = Clock ? n8_bit_register_bank_1_output_register_b : 8'bz;  // Controlled_Buffer controlled_buffer_13
  assign controlled_buffer_8_out = n8_bit_cu_1_alu ? ALU_output : 8'bz;  // Controlled_Buffer controlled_buffer_14
  _8_Bit_ALU ALU (
    .A(controlled_buffer_12_out), .B(controlled_buffer_13_out), .Compare(n8_bit_cu_1_com),
    .Sub(n8_bit_cu_1_sub), .Add(n8_bit_cu_1_add), .Dec(n8_bit_cu_1_dec), .Inc(n8_bit_cu_1_inc),
    .Not(n8_bit_cu_1_not), .And(n8_bit_cu_1_and), .Or(n8_bit_cu_1_orr), .Left(n8_bit_cu_1_slt),
    .Right(n8_bit_cu_1_srt), .Clock(Clock), .Output(ALU_output), .Carry(ALU_carry), .Overflow(ALU_overflow));
  or or_2 (or_2_out, ALU_carry, ALU_overflow);
  LED led_1 (.in(controlled_buffer_15_out));
  assign controlled_buffer_15_out = Clock ? or_2_out : 1'bz;  // Controlled_Buffer controlled_buffer_15
  _8_bit_equality u_8_bit_equality_1 (
    .A(n8_bit_register_bank_1_output_register_a), .B(8'h2), .Equal(n8_bit_equality_1_equal));  // open: Lesser, Greater
  and and_1 (and_1_out, n8_bit_equality_1_equal, n8_bit_cu_1_cjmp);

  // Notes on the sheet:
  //   SET
  //   CJMP
endmodule
